// Logisim project ALU.circ as structural Verilog: 1 circuit, main circuit main
module main (
  input  [7:0] X,
  input  [7:0] Y,
  input  [5:0] no_f_ny_zy_nx_zx,
  output zr,
  output [7:0] out_5,
  output ng
);

  wire or_1_out;
  wire [6:0] and_4_out;
  wire [7:0] adder_1_out, and_1_out, and_2_out, and_3_out, multiplexer_1_out, multiplexer_2_out,
       multiplexer_3_out, multiplexer_4_out, multiplexer_5_out, not_1_out, not_2_out, not_3_out;

  assign and_1_out = X & {8{1'b0}};  // AND_Gate and_1, 8 bits wide
  assign and_2_out = Y & {8{1'b0}};  // AND_Gate and_2, 8 bits wide
  Multiplexer #(.width(8), .enable("false")) multiplexer_1 (
    .in0(Y), .in1(and_2_out), .out(multiplexer_1_out), .sel(no_f_ny_zy_nx_zx[2]));
  Multiplexer #(.width(8), .enable("false")) multiplexer_2 (
    .in0(X), .in1(and_1_out), .out(multiplexer_2_out), .sel(no_f_ny_zy_nx_zx[0]));
  assign not_1_out = ~multiplexer_1_out;  // NOT_Gate not_1, 8 bits wide
  assign not_2_out = ~multiplexer_2_out;  // NOT_Gate not_2, 8 bits wide
  Multiplexer #(.width(8), .enable("false")) multiplexer_3 (
    .in0(multiplexer_1_out), .in1(not_1_out), .out(multiplexer_3_out), .sel(no_f_ny_zy_nx_zx[3]));
  Multiplexer #(.width(8), .enable("false")) multiplexer_4 (
    .in0(multiplexer_2_out), .in1(not_2_out), .out(multiplexer_4_out), .sel(no_f_ny_zy_nx_zx[1]));
  assign and_3_out = multiplexer_3_out & multiplexer_4_out;  // AND_Gate and_3, 8 bits wide
  Adder adder_1 (.a(multiplexer_3_out), .b(multiplexer_4_out), .out(adder_1_out));  // open: cin, cout
  Multiplexer #(.width(8), .enable("false")) multiplexer_5 (
    .in0(and_3_out), .in1(adder_1_out), .out(multiplexer_5_out), .sel(no_f_ny_zy_nx_zx[4]));
  assign not_3_out = ~multiplexer_5_out;  // NOT_Gate not_3, 8 bits wide
  Multiplexer #(.width(8), .enable("false")) multiplexer_6 (
    .in0(multiplexer_5_out), .in1(not_3_out), .out(out_5), .sel(no_f_ny_zy_nx_zx[5]));
  or or_1 (or_1_out, out_5[7], out_5[6], out_5[5], out_5[4], out_5[3], out_5[2], out_5[1], out_5[0]);
  not not_4 (zr, or_1_out);
  assign {ng, and_4_out} = {8{1'b1}} & out_5;  // AND_Gate and_4, 8 bits wide

  // Notes on the sheet:
  //   zy
  //   zx
  //   8 BIT ALU
  //   ny
  //   nx
  //   DESIGNED BY:
  //   [257] SHREYANSH JHA
  //   [264] VIBHU RASTOGI
  //   [265] AYUSH GUPTA
endmodule
